# Fritzing sketch Koblingsskjema (saved by Fritzing 0.9.5d)
circuit board: 8.46667cm x 5.64444cm
breadboards: 1

parts:
  Part1 = Arduino Mega 2560 (Rev3)
  U1 = LCD-16X2 [package=lcd-8x2]
  S1 = Pushbutton [package="[SMD]"]
  Q1 = LTR-301 [package=ltr-301]
  T1 = TMP36 Temperature Sensor [package="TO92 [THT]"]
  RHT1 = Humidity and Temperature Sensor RHT03
  LED1 = LED - 5mm [color="Red (633nm)" package="5 mm [THT]"]
  LED2 = LED - 5mm [color="Red (633nm)" package="5 mm [THT]"]
  LED3 = LED - 5mm [color="Red (633nm)" package="5 mm [THT]"]
  LED4 = LED - 5mm [color="Red (633nm)" package="5 mm [THT]"]
  R1 = Resistor [tolerance=±5% resistance=10k package=THT]
  R2 = Resistor [tolerance=±5% resistance=270 package=THT]
  R5 = Resistor [tolerance=±5% resistance=270 package=THT]
  R6 = Resistor [tolerance=±5% resistance=270 package=THT]
  R7 = Resistor [tolerance=±5% resistance=270 package=THT]
  R8 = Resistor [tolerance=±5% resistance=10k package=THT]
  S2 = Pushbutton [package="[SMD]"]
  R9 = Resistor [tolerance=±5% resistance=10k package=THT]
  S3 = Pushbutton [package="[SMD]"]
  R10 = Resistor [tolerance=±5% resistance=10k package=THT]
  S4 = Pushbutton [package="[SMD]"]
  R11 = Resistor [tolerance=±5% resistance=10k package=THT]
  J1 = Piezo Speaker
  R12 = Resistor [tolerance=±5% resistance=220 package=THT]
  R13 = Resistor [tolerance=±5% resistance=10k package=THT]

nets:
  N1: Part1.A0, T1.Vout
  N2: Part1.A5, Q1.E, R1.Pin_1
  5V: Part1.5V, U1.VDD, S1.Pin_3, S1.Pin_4, Q1.C, T1.+Vs, RHT1.Vcc, S2.Pin_3, S2.Pin_4, S3.Pin_3, S3.Pin_4, S4.Pin_3, S4.Pin_4, R13.Pin_0
  GND: Part1.GND, U1.VSS, U1.VO, U1.R_W, U1.K, T1.GND, RHT1.GND_2, R1.Pin_0, R2.Pin_1, R5.Pin_1, R6.Pin_1, R7.Pin_1, R8.Pin_1, R9.Pin_1, R10.Pin_1, R11.Pin_1, R12.Pin_0
  N3: Part1.D5_PWM, LED1.anode, LED2.anode
  N4: Part1.D6_PWM, LED3.anode, LED4.anode
  N5: Part1.D29, J1.pin1
  N6: Part1.D30, S4.Pin_1, S4.Pin_2, R11.Pin_0
  N7: Part1.D31, S3.Pin_1, S3.Pin_2, R10.Pin_0
  N8: Part1.D32, S2.Pin_1, S2.Pin_2, R9.Pin_0
  N9: Part1.D33, S1.Pin_1, S1.Pin_2, R8.Pin_0
  N10: Part1.D45, RHT1.Data-signal
  N11: Part1.D48, U1.DB7
  N12: Part1.D49, U1.DB6
  N13: Part1.D50, U1.DB5
  N14: Part1.D51, U1.DB4
  N15: Part1.D52, U1.E
  N16: Part1.D53, U1.RS
  N17: U1.A, R13.Pin_1
  N18: LED1.cathode, R2.Pin_0
  N19: LED2.cathode, R5.Pin_0
  N20: LED3.cathode, R6.Pin_0
  N21: LED4.cathode, R7.Pin_0
  N22: J1.pin2, R12.Pin_1
